// Logisim project cpu.circ as structural Verilog: 2 circuits, main circuit main
module main (
);

  ALU alu_1 ();  // open: A, B, S, out_4
endmodule

module ALU (
  input  [7:0] A,
  input  [7:0] B,
  input  [2:0] S,
  output [7:0] out_4
);

  wire [7:0] adder_1_out, and_1_out, multiplexer_1_out, not_1_out, or_1_out;

  assign not_1_out = ~B;  // NOT_Gate not_1, 8 bits wide
  Multiplexer #(.width(8)) multiplexer_1 (.in0(B), .in1(not_1_out), .out(multiplexer_1_out), .sel(S[2]));
  assign and_1_out = A & B;  // AND_Gate and_1, 8 bits wide
  assign or_1_out = A | B;  // OR_Gate or_1, 8 bits wide
  Adder adder_1 (.a(A), .b(multiplexer_1_out), .out(adder_1_out), .cin(S[2]));  // open: cout
  Multiplexer #(.select(2), .width(8)) multiplexer_2 (
    .in0(adder_1_out), .in1(and_1_out), .in2(or_1_out), .in3(A), .out(out_4), .sel(S[1:0]));
endmodule
